# Fritzing sketch RoboLed (saved by Fritzing 0.9.3b)
circuit board: 5.72018cm x 4.6133cm
breadboards: 1

parts:
  R1 = Resistor [tolerance=±5% resistance=10k package=THT]
  Part1 = Arduino Uno (Rev3)
  M1 = DC Motor [part_number=Fan]
  D1 = Rectifier Diode [part_number=1N4001 package="300 mil [THT]"]
  C1 = Electrolytic Capacitor [capacitance=47µF voltage=35V package="100 mil [THT, electrolytic]"]
  R2 = Resistor [tolerance=±5% resistance=3.3k package=THT]
  DRV_1 = DRV 8825 Stepper Motor Carrier, High Current [part_number="DRV 8825"]
  U1 = TMP36 [part_number=KY028 package=to-92-kit]
  Q3 = NPN-Transistor [part_number=2N3904 package="TO92 [THT]"]
  Q1 = npn-Powertransistor [part_number=BD137 package="TO220 [THT]"]
  R3 = Resistor [tolerance=±5% resistance=100 package=THT]
  Q2 = pnp-Powertransistor [part_number=D45H11 package="TO220 [THT]"]
  LEDLamp = LED - 5mm [color="White (8000K)" package="5 mm [THT]"]
  C2 = Ceramic Capacitor [capacitance=47nF package="100 mil [THT, multilayer]"]
  J2 = male pin header, 4 pins [form="♂ (male)"]
  J4 = male pin header, 1 pin [form="♂ (male)"]
  J5 = male pin header, 1 pin [form="♂ (male)"]
  J3 = male pin header, 3 pins [form="♂ (male)"]
  J1 = male pin header, 2 pins [form="♂ (male)"]
  J6 = male pin header, 1 pin [form="♂ (male)"]
  MOTOR1 = Adafruit Gear-Reduced Stepper Motor (small)  # not connected
  M2 = Dagu DGServo 9g (Pan and tilt) [part_number=SG90]
  R4 = Rotary Potentiometer (Small) [maximum_resistance=5kΩ package=THT]
  LM1 = RioRand LM2596  # not connected

nets (from the schematic view):
  N1: R1.Pin_0, Part1.D9_PWM, J5.pin1
  N2: R1.Pin_1, Q1.base
  N3: Part1.A0, U1.VOUT
  N4: Part1.A1, R4.wiper
  GND: Part1.GND, C1.-, DRV_1.GROUND_ST/_MT, DRV_1.GROUND_LOG, U1.GND, Q3.E, Q1.emitter, LEDLamp.cathode, C2.0, J1.pin2, M2.gnd, R4.leg1
  N5: Part1.D2, DRV_1.STEP, J3.pin2
  N6: Part1.D3_PWM, R2.Pin_0, J4.pin1
  N7: Part1.D4, DRV_1.DIRECTION, J3.pin3
  N8: Part1.D6_PWM, M2.pulse
  VCC: Part1.5V, U1.VCC, M2.vcc, R4.leg2
  12V: M1.pin_1, D1.cathode, C1.+, DRV_1.VOLTAGE_ST/_MT, J1.pin1
  N9: M1.pin_2, D1.anode, Q1.collector
  N10: R2.Pin_1, Q3.B
  5V: DRV_1.RESET, DRV_1.SLEEP, J3.pin1
  N11: DRV_1.OUT_2B, J2.pin1
  N12: DRV_1.OUT_2A, J2.pin2
  N13: DRV_1.OUT_1A, J2.pin3
  N14: DRV_1.OUT_1B, J2.pin4
  N15: Q3.C, R3.Pin_0
  N16: R3.Pin_1, Q2.base, C2.1
  N17: Q2.collector, LEDLamp.anode
  30V: Q2.emitter, J6.pin1

custom parts:
  Adafruit Gear-Reduced Stepper Motor (small): Adafruit gear-reduction stepper motor (small)
